# Fritzing sketch Arduino pro mini shield principle schem (saved by Fritzing 0.9.2b)

parts:
  Part1 = Arduino Pro Mini v13
  LCD1 = LCD screen
  U1 = mystery part, 3 pins [chip_label="5 to 3.3V"]
  ANT1 = Antenna  # not connected
  U3 = mystery part, 8 pins [chip_label=NRF24L01]
  J2 = female pin header, 3 pins [form="♀ (female)"]
  J1 = male pin header, 2 pins [form="♂ (male)"]
  R1 = Trimmer Potentiometer [maximum_resistance=10kΩ package=THT]
  led = LED - 5mm [color="Red (633nm)" package="5 mm [THT]"]
  K1 = Relay [part_number=FRS1B-S package=THT]
  jmp2 = male pin header, 2 pins [form="♂ (male)"]
  S1 = Pushbutton [package=THT]
  J6 = female pin header, 2 pins [form="♀ (female)"]
  J15 = male pin header, 3 pins [form="♂ (male)"]  # not connected
  Rl = Resistor [tolerance=±5% resistance=220 package=THT]
  J4 = female pin header, 5 pins [form="♀ (female)"]
  J5 = male pin header, 5 pins [form="♂ (male)"]
  J6_2 = mystery part, 6 pins [chip_label=?]
  R = Resistor [tolerance=±5% resistance=10k package=THT]
  C = Tantalum Capacitor [capacitance=47µF package="100 mil [THT, tantalum]"]  # not connected
  D1 = Zener Diode [part_number=1N4732A breakdown_voltage=5.1V package="300 mil [THT]"]
  C1 = Tantalum Capacitor [capacitance=1pF package="100 mil [THT, tantalum]"]
  R2 = Resistor [tolerance=±5% resistance=0 package=THT]
  J16 = screw terminal, 3 pins
  J19 = screw terminal, 3 pins  # not connected
  J5_2 = male pin header, 3 pins [form="♂ (male)"]
  jmp3 = male pin header, 2 pins [form="♂ (male)"]

nets:
  N1: Part1.RAW, U1.pin1, J4.pin1, J6_2.pin1, J5_2.pin3
  N2: Part1.GND, J1.pin1, D1.anode
  N3: Part1.RESET, jmp2.pin1
  VCC: Part1.VCC, LCD1.VDD, J2.pin2
  N4: Part1.A3, jmp2.pin2, J4.pin5, jmp3.pin2
  N5: Part1.A2, J4.pin4
  N6: Part1.A1, J4.pin3
  N7: Part1.A0, D1.cathode, C1.+, R2.Pin_1
  N8: Part1.D13/SCK, Part1.D9_PWM, U3.pin3, U3.pin7
  N9: Part1.D8, Part1.D7, LCD1.DB6, LCD1.DB7
  N10: Part1.D6_PWM, LCD1.LED+
  N11: Part1.D5_PWM, Part1.D4, LCD1.DB4, LCD1.DB5
  N12: Part1.D3_PWM, LCD1.E
  5V: Part1.D2, LCD1.RS
  N13: LCD1.V0, R1.wiper
  N14: LCD1.LED-, J1.pin2
  N15: U1.pin3, U3.pin2
  N16: J2.pin3, R.Pin_1, R2.Pin_0
  N17: led.cathode, jmp3.pin1
  N18: led.anode, Rl.Pin_1
  N19: K1.A, J16.pin1
  N20: K1.COIL1, J5.pin3
  N21: K1.C1, K1.C2, J16.pin2
  N22: K1.B, J16.pin3
  N23: S1.leg0, J6.pin2
  N24: S1.leg1, J6.pin1
  N25: R.Pin_0, C1.-
  N26: J5_2.pin1, J5_2.pin2

notes:
  5 to 3.3V
  NRF24L01+
  See only Schematic overview, PCB in separate file
  PCB in separate Fritzing file
  Many connections to GND and +5V are not shown
  valve
  pump motor
  230 V
  optional
  USB to DIP
  NO
  NC
  Optional/Unused
  Arduino pro mini shield
  Principle schem
  jmp1a
  jmp4a
  +5V
  GND
  - - - - - - - - - -
  jmp1b
  jmp4b
  Some parallel wires to parts are drawn as 1 line.

custom parts:
  Arduino Pro Mini v13: It's blue! It's thin! It's the Arduino Pro Mini! SparkFun's minimal design approach to Arduino. This is a 5V Arduino running the 16MHz bootloader. Arduino Pro Mini does not come with connectors populated so that you can solder in any connector or wire with any orientation you need. We recommend first time Arduino users start with the Uno R3. It's a great board that will get you up and running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
